// Logisim project mips_processor.circ as structural Verilog: 7 circuits, main circuit main
module main (
  output [31:0] out_1,
  output [31:0] out_2
);

  wire alu_1_zero_flag, and_1_out, clock_1_out, control_unit_1_alusrc, control_unit_1_branch,
       control_unit_1_memread, control_unit_1_memtoreg, control_unit_1_memwrite, control_unit_1_regdst,
       control_unit_1_regwrite;
  wire [1:0] control_unit_1_aluop;
  wire [3:0] alu_control_1_alucontrol__3_0;
  wire [4:0] multiplexer_1_out;
  wire [31:0] adder_1_out, adder_2_out, alu_1_output, multiplexer_2_out, multiplexer_3_out,
       multiplexer_4_out, PC_q, registers_1_readdata1, registers_1_readdata2, shift_left_by_2_1_out32,
       sign_extend_1_immediate_32bits;

  Register #(.width(32)) PC (.D(multiplexer_3_out), .en(1'b1), .Q(PC_q), .clk(clock_1_out), .clr(1'b0));
  Clock clock_1 (.out(clock_1_out));
  Adder #(.width(32)) adder_1 (.a(PC_q), .b(32'h4), .out(adder_1_out));  // open: cin, cout
  RAM #(.addrWidth(10), .dataWidth(32), .bus("asynch")) ram_1 (
    .addr(PC_q[11:2]), .data(out_2), .sel(1'b1), .ld(1'b1), .clr(1'b0));
  Registers registers_1 (
    .RegWrite(control_unit_1_regwrite), .WriteReg(multiplexer_1_out), .ReadData1(registers_1_readdata1),
    .ReadReg1(out_2[25:21]), .ReadData2(registers_1_readdata2), .ReadReg2(out_2[20:16]),
    .WriteData(multiplexer_4_out), .Clock(clock_1_out));
  Multiplexer #(.width(5), .enable("false")) multiplexer_1 (
    .in0(out_2[20:16]), .in1(out_2[15:11]), .out(multiplexer_1_out), .sel(control_unit_1_regdst));
  Control_Unit control_unit_1 (
    .RegDst(control_unit_1_regdst), .Opcode__5_0(out_2[31:26]), .ALUSrc(control_unit_1_alusrc),
    .RegWrite(control_unit_1_regwrite), .Branch(control_unit_1_branch), .MemRead(control_unit_1_memread),
    .MemtoReg(control_unit_1_memtoreg), .MemWrite(control_unit_1_memwrite), .ALUOp(control_unit_1_aluop));
  Sign_Extend sign_extend_1 (.immediate_16bits(out_2[15:0]), .immediate_32bits(sign_extend_1_immediate_32bits));
  shift_left_by_2 shift_left_by_2_1 (.In32(sign_extend_1_immediate_32bits), .Out32(shift_left_by_2_1_out32));
  Multiplexer #(.width(32), .enable("false")) multiplexer_2 (
    .in0(registers_1_readdata2), .in1(sign_extend_1_immediate_32bits), .out(multiplexer_2_out),
    .sel(control_unit_1_alusrc));
  ALU_Control alu_control_1 (
    .funct__5_0(out_2[5:0]), .ALUControl__3_0(alu_control_1_alucontrol__3_0),
    .ALUOp__1_0(control_unit_1_aluop), .opcode__5_0(out_2[31:26]));
  Multiplexer #(.width(32), .enable("false")) multiplexer_3 (
    .in0(adder_1_out), .in1(adder_2_out), .out(multiplexer_3_out), .sel(and_1_out));
  Adder #(.width(32)) adder_2 (.a(adder_1_out), .b(shift_left_by_2_1_out32), .out(adder_2_out));  // open: cin, cout
  and and_1 (and_1_out, control_unit_1_branch, alu_1_zero_flag);
  ALU alu_1 (
    .ReadData1(registers_1_readdata1), .ReadData2(multiplexer_2_out), .Zero_Flag(alu_1_zero_flag),
    .Output(alu_1_output), .ALUControl__3_0(alu_control_1_alucontrol__3_0));
  RAM #(.addrWidth(10), .dataWidth(32), .bus("separate")) ram_2 (
    .addr(alu_1_output[11:2]), .din(registers_1_readdata2), .data(out_1), .str(control_unit_1_memwrite),
    .sel(1'b1), .clk(clock_1_out), .ld(control_unit_1_memread), .clr(1'b0));
  Multiplexer #(.width(32), .enable("false")) multiplexer_4 (
    .in0(alu_1_output), .in1(out_1), .out(multiplexer_4_out), .sel(control_unit_1_memtoreg));

  // Notes on the sheet:
  //   Instruction Memory
  //   Instruction [31:26]
  //   RegDst
  //   Write
  //   data
  //   \
  //   16
  //   Read Register 1
  //   Read Register 2
  //   Write Register
  //   ALUSrc
  //   Branch
  //   ALUOp
  //   MemRead
  //   MemtoReg
  //   MemWrite
  //   RegWrite
  //   Read
  //   data 1
  //   Read
  //   data 2
  //   \
  //   32
  //   Zero
  //   ALU
  //   result
  //   Data Memory
endmodule

module Control_Unit (
  input  [5:0] Opcode__5_0,
  output RegDst,
  output ALUSrc,
  output [1:0] ALUOp,
  output RegWrite,
  output Branch,
  output MemRead,
  output MemtoReg,
  output MemWrite
);

  wire addi_out, andi_out, not_1_out, not_2_out, not_3_out, not_4_out, not_5_out, not_6_out, not_7_out,
       not_8_out, not_9_out, not_10_out, not_11_out, not_12_out, not_13_out, not_14_out, not_15_out,
       not_16_out, not_17_out, not_18_out, not_19_out, not_20_out, not_21_out, not_22_out, not_23_out,
       not_24_out, not_25_out, not_26_out, not_27_out, not_28_out, ori_out;

  not not_1 (not_1_out, Opcode__5_0[0]);
  not not_2 (not_2_out, Opcode__5_0[4]);
  not not_3 (not_3_out, Opcode__5_0[0]);
  not not_4 (not_4_out, Opcode__5_0[1]);
  not not_5 (not_5_out, Opcode__5_0[2]);
  not not_6 (not_6_out, Opcode__5_0[3]);
  not not_7 (not_7_out, Opcode__5_0[4]);
  not not_8 (not_8_out, Opcode__5_0[5]);
  not not_9 (not_9_out, Opcode__5_0[0]);
  not not_10 (not_10_out, Opcode__5_0[1]);
  not not_11 (not_11_out, Opcode__5_0[2]);
  not not_12 (not_12_out, Opcode__5_0[4]);
  not not_13 (not_13_out, Opcode__5_0[5]);
  not not_14 (not_14_out, Opcode__5_0[0]);
  not not_15 (not_15_out, Opcode__5_0[1]);
  not not_16 (not_16_out, Opcode__5_0[4]);
  not not_17 (not_17_out, Opcode__5_0[5]);
  not not_18 (not_18_out, Opcode__5_0[1]);
  not not_19 (not_19_out, Opcode__5_0[4]);
  not not_20 (not_20_out, Opcode__5_0[5]);
  not not_21 (not_21_out, Opcode__5_0[1]);
  not not_22 (not_22_out, Opcode__5_0[3]);
  not not_23 (not_23_out, Opcode__5_0[5]);
  not not_24 (not_24_out, Opcode__5_0[2]);
  not not_25 (not_25_out, Opcode__5_0[3]);
  not not_26 (not_26_out, Opcode__5_0[4]);
  not not_27 (not_27_out, Opcode__5_0[4]);
  not not_28 (not_28_out, Opcode__5_0[2]);
  and R_Type (ALUOp[1], not_3_out, not_4_out, not_5_out, not_6_out, not_7_out, not_8_out);
  and addi (addi_out, not_9_out, not_10_out, not_11_out, Opcode__5_0[3], not_12_out, not_13_out);
  and andi (andi_out, not_14_out, not_15_out, Opcode__5_0[2], Opcode__5_0[3], not_16_out, not_17_out);
  and ori (ori_out, Opcode__5_0[0], not_18_out, Opcode__5_0[2], Opcode__5_0[3], not_19_out, not_20_out);
  and beq (ALUOp[0], not_1_out, not_21_out, Opcode__5_0[2], not_22_out, not_2_out, not_23_out);
  and lw (MemRead, Opcode__5_0[0], Opcode__5_0[1], not_24_out, not_25_out, not_26_out, Opcode__5_0[5]);
  and sw (MemWrite, Opcode__5_0[0], Opcode__5_0[1], not_28_out, Opcode__5_0[3], not_27_out, Opcode__5_0[5]);
  or or_1 (ALUSrc, addi_out, andi_out, ori_out, MemRead, MemWrite);
  or or_2 (RegWrite, ALUOp[1], ALUSrc, MemRead);

  assign Branch = ALUOp[0];
  assign MemtoReg = MemRead;
  assign RegDst = ALUOp[1];
endmodule

module ALU_Control (
  input  [5:0] funct__5_0,
  input  [1:0] ALUOp__1_0,
  input  [5:0] opcode__5_0,
  output [3:0] ALUControl__3_0
);

  wire decoder_1_out0, decoder_1_out2, decoder_1_out5, decoder_1_out10, not_1_out, not_2_out, not_3_out,
       not_4_out, not_5_out, not_6_out, not_7_out;
  wire [0:0] ori_out;
  wire [2:0] or_1_out;

  Decoder #(.select(4), .enable("false")) decoder_1 (
    .out0(decoder_1_out0), .out2(decoder_1_out2), .out5(decoder_1_out5), .out10(decoder_1_out10),
    .sel(funct__5_0[3:0]));  // open: out1, out3, out4, out6, out7, out8, out9, out11, out12, out13, out14, out15
  not not_1 (not_1_out, opcode__5_0[1]);
  not not_2 (not_2_out, opcode__5_0[0]);
  not not_3 (not_3_out, opcode__5_0[4]);
  not not_4 (not_4_out, opcode__5_0[5]);
  or or_1 (or_1_out[0], decoder_1_out5, decoder_1_out10);
  or or_2 (or_1_out[1], decoder_1_out0, decoder_1_out2, decoder_1_out10);
  or or_3 (or_1_out[2], decoder_1_out2, decoder_1_out10);
  not not_5 (not_5_out, opcode__5_0[1]);
  not not_6 (not_6_out, opcode__5_0[4]);
  not not_7 (not_7_out, opcode__5_0[5]);
  // AND_Gate andi has open pins: in0=not_2_out, in1=not_5_out, in2=opcode__5_0[2], in3=opcode__5_0[3], in4=not_6_out, in5=not_7_out, out=open
  and ori (ori_out[0], opcode__5_0[0], not_1_out, opcode__5_0[2], opcode__5_0[3], not_3_out, not_4_out);
  Multiplexer #(.select(2), .width(4), .enable("false")) multiplexer_1 (
    .in0(4'b0010), .in1(4'b0110), .in2({1'b0, or_1_out}), .in3({3'b000, ori_out[0]}), .out(ALUControl__3_0),
    .sel(ALUOp__1_0));

  // Notes on the sheet:
  //   addi
  //   beq
endmodule

module shift_left_by_2 (
  input  [31:0] In32,
  output [31:0] Out32
);


  assign Out32 = {In32[29:0], 2'b00};
endmodule

module Registers (
  input  [31:0] WriteData,
  input  [4:0] ReadReg1,
  input  RegWrite,
  input  [4:0] WriteReg,
  input  Clock,
  input  [4:0] ReadReg2,
  output [31:0] ReadData1,
  output [31:0] ReadData2
);

  wire decoder_1_out1, decoder_1_out2, decoder_1_out3, decoder_1_out4, decoder_1_out5, decoder_1_out6,
       decoder_1_out7, decoder_1_out8, decoder_1_out9, decoder_1_out10, decoder_1_out11, decoder_1_out12,
       decoder_1_out13, decoder_1_out14, decoder_1_out15, decoder_1_out16, decoder_1_out17, decoder_1_out18,
       decoder_1_out19, decoder_1_out20, decoder_1_out21, decoder_1_out22, decoder_1_out23, decoder_1_out24,
       decoder_1_out25, decoder_1_out26, decoder_1_out27, decoder_1_out28, decoder_1_out29, decoder_1_out30,
       decoder_1_out31;
  wire [31:0] _1_q, _2_q, _3_q, _4_q, _5_q, _6_q, _7_q, _8_q, _9_q, _10_q, _11_q, _12_q, _13_q, _14_q, _15_q,
       _16_q, _17_q, _18_q, _19_q, _20_q, _21_q, _22_q, _23_q, _24_q, _25_q, _26_q, _27_q, _28_q, _29_q,
       _30_q, _31_q;

  Decoder #(.select(5)) decoder_1 (
    .out1(decoder_1_out1), .out2(decoder_1_out2), .out3(decoder_1_out3), .out4(decoder_1_out4),
    .out5(decoder_1_out5), .out6(decoder_1_out6), .out7(decoder_1_out7), .out8(decoder_1_out8),
    .out9(decoder_1_out9), .out10(decoder_1_out10), .out11(decoder_1_out11), .out12(decoder_1_out12),
    .out13(decoder_1_out13), .out14(decoder_1_out14), .out15(decoder_1_out15), .out16(decoder_1_out16),
    .out17(decoder_1_out17), .out18(decoder_1_out18), .out19(decoder_1_out19), .out20(decoder_1_out20),
    .out21(decoder_1_out21), .out22(decoder_1_out22), .out23(decoder_1_out23), .out24(decoder_1_out24),
    .out25(decoder_1_out25), .out26(decoder_1_out26), .out27(decoder_1_out27), .out28(decoder_1_out28),
    .out29(decoder_1_out29), .out30(decoder_1_out30), .out31(decoder_1_out31), .sel(WriteReg), .en(RegWrite));  // open: out0
  Register #(.width(32)) _8 (.D(WriteData), .en(decoder_1_out8), .Q(_8_q), .clk(Clock));  // open: clr
  Register #(.width(32)) _16 (.D(WriteData), .en(decoder_1_out16), .Q(_16_q), .clk(Clock));  // open: clr
  Register #(.width(32)) _24 (.D(WriteData), .en(decoder_1_out24), .Q(_24_q), .clk(Clock));  // open: clr
  Register #(.width(32)) _1 (.en(decoder_1_out1), .Q(_1_q), .clk(Clock));  // open: D, clr
  Register #(.width(32)) _9 (.D(WriteData), .en(decoder_1_out9), .Q(_9_q), .clk(Clock));  // open: clr
  Register #(.width(32)) _17 (.D(WriteData), .en(decoder_1_out17), .Q(_17_q), .clk(Clock));  // open: clr
  Register #(.width(32)) _25 (.D(WriteData), .en(decoder_1_out25), .Q(_25_q), .clk(Clock));  // open: clr
  Register #(.width(32)) _2 (.D(WriteData), .en(decoder_1_out2), .Q(_2_q), .clk(Clock));  // open: clr
  Register #(.width(32)) _10 (.D(WriteData), .en(decoder_1_out10), .Q(_10_q), .clk(Clock));  // open: clr
  Register #(.width(32)) _18 (.D(WriteData), .en(decoder_1_out18), .Q(_18_q), .clk(Clock));  // open: clr
  Register #(.width(32)) _26 (.D(WriteData), .en(decoder_1_out26), .Q(_26_q), .clk(Clock));  // open: clr
  Register #(.width(32)) _3 (.D(WriteData), .en(decoder_1_out3), .Q(_3_q), .clk(Clock));  // open: clr
  Register #(.width(32)) _11 (.D(WriteData), .en(decoder_1_out11), .Q(_11_q), .clk(Clock));  // open: clr
  Register #(.width(32)) _19 (.D(WriteData), .en(decoder_1_out19), .Q(_19_q), .clk(Clock));  // open: clr
  Register #(.width(32)) _27 (.D(WriteData), .en(decoder_1_out27), .Q(_27_q), .clk(Clock));  // open: clr
  Register #(.width(32)) _4 (.D(WriteData), .en(decoder_1_out4), .Q(_4_q), .clk(Clock));  // open: clr
  Register #(.width(32)) _12 (.D(WriteData), .en(decoder_1_out12), .Q(_12_q), .clk(Clock));  // open: clr
  Register #(.width(32)) _20 (.D(WriteData), .en(decoder_1_out20), .Q(_20_q), .clk(Clock));  // open: clr
  Register #(.width(32)) _28 (.D(WriteData), .en(decoder_1_out28), .Q(_28_q), .clk(Clock));  // open: clr
  Register #(.width(32)) _5 (.D(WriteData), .en(decoder_1_out5), .Q(_5_q), .clk(Clock));  // open: clr
  Register #(.width(32)) _13 (.D(WriteData), .en(decoder_1_out13), .Q(_13_q), .clk(Clock));  // open: clr
  Register #(.width(32)) _21 (.D(WriteData), .en(decoder_1_out21), .Q(_21_q), .clk(Clock));  // open: clr
  Register #(.width(32)) _29 (.D(WriteData), .en(decoder_1_out29), .Q(_29_q), .clk(Clock));  // open: clr
  Register #(.width(32)) _6 (.D(WriteData), .en(decoder_1_out6), .Q(_6_q), .clk(Clock));  // open: clr
  Register #(.width(32)) _14 (.D(WriteData), .en(decoder_1_out14), .Q(_14_q), .clk(Clock));  // open: clr
  Register #(.width(32)) _22 (.D(WriteData), .en(decoder_1_out22), .Q(_22_q), .clk(Clock));  // open: clr
  Register #(.width(32)) _30 (.D(WriteData), .en(decoder_1_out30), .Q(_30_q), .clk(Clock));  // open: clr
  Register #(.width(32)) _7 (.D(WriteData), .en(decoder_1_out7), .Q(_7_q), .clk(Clock));  // open: clr
  Register #(.width(32)) _15 (.D(WriteData), .en(decoder_1_out15), .Q(_15_q), .clk(Clock));  // open: clr
  Register #(.width(32)) _23 (.D(WriteData), .en(decoder_1_out23), .Q(_23_q), .clk(Clock));  // open: clr
  Register #(.width(32)) _31 (.D(WriteData), .en(decoder_1_out31), .Q(_31_q), .clk(Clock));  // open: clr
  Multiplexer #(.select(5), .width(32), .enable("false")) multiplexer_1 (
    .in0({32{1'b0}}), .in1(_1_q), .in2(_2_q), .in3(_3_q), .in4(_4_q), .in5(_5_q), .in6(_6_q), .in7(_7_q),
    .in8(_8_q), .in9(_9_q), .in10(_10_q), .in11(_11_q), .in12(_12_q), .in13(_13_q), .in14(_14_q),
    .in15(_15_q), .in16(_16_q), .in17(_17_q), .in18(_18_q), .in19(_19_q), .in20(_20_q), .in21(_21_q),
    .in22(_22_q), .in23(_23_q), .in24(_24_q), .in25(_25_q), .in26(_26_q), .in27(_27_q), .in28(_28_q),
    .in29(_29_q), .in30(_30_q), .in31(_31_q), .out(ReadData1), .sel(ReadReg1));
  Multiplexer #(.select(5), .width(32), .enable("false")) multiplexer_2 (
    .in0({32{1'b0}}), .in1(_1_q), .in2(_2_q), .in3(_3_q), .in4(_4_q), .in5(_5_q), .in6(_6_q), .in7(_7_q),
    .in8(_8_q), .in9(_9_q), .in10(_10_q), .in11(_11_q), .in12(_12_q), .in13(_13_q), .in14(_14_q),
    .in15(_15_q), .in16(_16_q), .in17(_17_q), .in18(_18_q), .in19(_19_q), .in20(_20_q), .in21(_21_q),
    .in22(_22_q), .in23(_23_q), .in24(_24_q), .in25(_25_q), .in26(_26_q), .in27(_27_q), .in28(_28_q),
    .in29(_29_q), .in30(_30_q), .in31(_31_q), .out(ReadData2), .sel(ReadReg2));
endmodule

module ALU (
  input  [31:0] ReadData1,
  input  [31:0] ReadData2,
  input  [3:0] ALUControl__3_0,
  output Zero_Flag,
  output [31:0] Output
);

  wire [31:0] adder_1_out, And_result_out, multiplexer_1_out, Or_result_out, subtractor_1_out;

  Adder #(.width(32)) adder_1 (.a(ReadData1), .b(ReadData2), .out(adder_1_out), .cin(1'b0));  // open: cout
  assign And_result_out = ReadData1 & ReadData2;  // AND_Gate And_result, 32 bits wide
  Subtractor #(.width(32)) subtractor_1 (.a(ReadData1), .b(ReadData2), .out(subtractor_1_out));  // open: bin, bout
  assign Or_result_out = ReadData1 | ReadData2;  // OR_Gate Or_result, 32 bits wide
  Multiplexer #(.width(32), .enable("false")) multiplexer_1 (
    .in0({32{1'b0}}), .in1(32'h1), .out(multiplexer_1_out), .sel(subtractor_1_out[31]));
  Multiplexer #(.select(4), .width(32), .enable("false")) multiplexer_2 (
    .in0(And_result_out), .in1(Or_result_out), .in2(adder_1_out), .in3({32{1'b0}}), .in4({32{1'b0}}),
    .in5({32{1'b0}}), .in6(subtractor_1_out), .in7(multiplexer_1_out), .in8({32{1'b0}}), .in9({32{1'b0}}),
    .in10({32{1'b0}}), .in11({32{1'b0}}), .in12({32{1'b0}}), .in13({32{1'b0}}), .in14({32{1'b0}}),
    .in15({32{1'b0}}), .out(Output), .sel(ALUControl__3_0));
  nor nor_1 (Zero_Flag, Output[0], Output[1], Output[2], Output[3], Output[4], Output[5], Output[6], Output[7], Output[8], Output[9], Output[10], Output[11], Output[12], Output[13], Output[14], Output[15], Output[16], Output[17], Output[18], Output[19], Output[20], Output[21], Output[22], Output[23], Output[24], Output[25], Output[26], Output[27], Output[28], Output[29], Output[30], Output[31]);
endmodule

module Sign_Extend (
  input  [15:0] immediate_16bits,
  output [31:0] immediate_32bits
);

  assign immediate_32bits = {{16{immediate_16bits[15]}}, immediate_16bits};  // Bit_Extender bit_extender_1
endmodule
